// Logisim project flappyBird.circ as structural Verilog: 10 circuits, main circuit main
module main (
  input  RESET,
  input  PLAY
);

  wire and_2_out, clock_1_out, comparator_1_eq, contatori_1_out_3, d_ff_1_q, game_over_1_out_3;
  wire [6:0] keyboard_1_data;
  wire [7:0] and_1_out, contatori_1_out_4, contatori_1_out_5, flappy_1_out_4, multiplexers_1_out_4,
       multiplexers_1_out_5, multiplexers_1_out_6, multiplexers_1_out_7, multiplexers_1_out_8,
       multiplexers_1_out_9, multiplexers_1_out_10, multiplexers_1_out_11, multiplexers_1_out_12,
       multiplexers_1_out_13, multiplexers_1_out_14, multiplexers_1_out_15, multiplexers_1_out_16,
       multiplexers_1_out_17, multiplexers_1_out_18, multiplexers_1_out_19, or_1_out, punti_1_out_2,
       punti_1_out_3, punti_1_out_4, punti_1_out_5, punti_1_out_6, punti_1_out_7, punti_2_out_2,
       punti_2_out_3, punti_2_out_4, punti_2_out_5, punti_2_out_6, punti_2_out_7;
  wire [7:7] not_1_out;

  Clock clock_1 (.out(clock_1_out));
  Keyboard keyboard_1 (.clk(clock_1_out), .data(keyboard_1_data));  // open: re, clr, avail
  Comparator #(.width(7)) comparator_1 (.a(keyboard_1_data), .b(7'b0001010), .eq(comparator_1_eq));  // open: gt, lt
  flappy flappy_1 (.PLAY(PLAY), .TASTIERA(comparator_1_eq), .Vittoria(contatori_1_out_3), .out_4(flappy_1_out_4));
  assign and_1_out = flappy_1_out_4 & {8{not_1_out[7]}};  // AND_Gate and_1, 8 bits wide
  assign or_1_out = multiplexers_1_out_17 | and_1_out;  // OR_Gate or_1, 8 bits wide
  punti punti_1 (
    .in_1(contatori_1_out_4), .out_2(punti_1_out_2), .out_3(punti_1_out_3), .out_4(punti_1_out_4),
    .out_5(punti_1_out_5), .out_6(punti_1_out_6), .out_7(punti_1_out_7));
  DotMatrix #(.matrixcols(6), .matrixrows(8)) dotmatrix_1 (
    .col0(punti_2_out_2), .col1(punti_2_out_3), .col2(punti_2_out_4), .col3(punti_2_out_5),
    .col4(punti_2_out_6), .col5(punti_2_out_7));
  DotMatrix #(.matrixcols(6), .matrixrows(8)) dotmatrix_2 (
    .col0(punti_1_out_2), .col1(punti_1_out_3), .col2(punti_1_out_4), .col3(punti_1_out_5),
    .col4(punti_1_out_6), .col5(punti_1_out_7));
  punti punti_2 (
    .in_1(contatori_1_out_5), .out_2(punti_2_out_2), .out_3(punti_2_out_3), .out_4(punti_2_out_4),
    .out_5(punti_2_out_5), .out_6(punti_2_out_6), .out_7(punti_2_out_7));
  contatori contatori_1 (
    .in_2(multiplexers_1_out_18), .in_1(RESET), .out_4(contatori_1_out_4), .out_5(contatori_1_out_5),
    .out_3(contatori_1_out_3));
  DotMatrix #(.matrixcols(16), .matrixrows(8)) dotmatrix_3 (
    .col0(multiplexers_1_out_19), .col1(multiplexers_1_out_18), .col2(or_1_out),
    .col3(multiplexers_1_out_16), .col4(multiplexers_1_out_15), .col5(multiplexers_1_out_14),
    .col6(multiplexers_1_out_13), .col7(multiplexers_1_out_12), .col8(multiplexers_1_out_11),
    .col9(multiplexers_1_out_10), .col10(multiplexers_1_out_9), .col11(multiplexers_1_out_8),
    .col12(multiplexers_1_out_7), .col13(multiplexers_1_out_6), .col14(multiplexers_1_out_5),
    .col15(multiplexers_1_out_4));
  multiplexers multiplexers_1 (
    .VINTO(contatori_1_out_3), .RESET(RESET), .PERSO(d_ff_1_q), .out_4(multiplexers_1_out_4),
    .out_5(multiplexers_1_out_5), .out_6(multiplexers_1_out_6), .out_7(multiplexers_1_out_7),
    .out_8(multiplexers_1_out_8), .out_9(multiplexers_1_out_9), .out_10(multiplexers_1_out_10),
    .out_11(multiplexers_1_out_11), .out_12(multiplexers_1_out_12), .out_13(multiplexers_1_out_13),
    .out_14(multiplexers_1_out_14), .out_15(multiplexers_1_out_15), .out_16(multiplexers_1_out_16),
    .out_17(multiplexers_1_out_17), .out_18(multiplexers_1_out_18), .out_19(multiplexers_1_out_19));
  game_over game_over_1 (.in_1(multiplexers_1_out_16), .in_2(flappy_1_out_4), .out_3(game_over_1_out_3));
  D_Flip_Flop d_ff_1 (.clk(and_2_out), .D(game_over_1_out_3), .Q(d_ff_1_q), .reset(RESET));  // open: Qn, preset, en
  and and_2 (and_2_out, not_1_out[7], clock_1_out);
  not not_1 (not_1_out[7], d_ff_1_q);

  // Notes on the sheet:
  //   ENTER
endmodule

module flappy (
  input  PLAY,
  input  TASTIERA,
  input  Vittoria,
  output [7:0] out_4
);

  wire clock_1_out, not_1_out;
  wire [1:0] multiplexer_1_out;
  wire [2:0] counter_1_q;

  Clock clock_1 (.out(clock_1_out));
  Multiplexer #(.select(2), .width(2)) multiplexer_1 (
    .in0(2'b10), .in1(2'b11), .in2(2'b01), .out(multiplexer_1_out), .sel({TASTIERA, PLAY}));  // open: in3, en
  Counter #(.width(3), .max('h7)) counter_1 (
    .load(multiplexer_1_out[1]), .D(3'b011), .count(multiplexer_1_out[0]), .Q(counter_1_q), .clk(clock_1_out));  // open: carry, clr
  not not_1 (not_1_out, Vittoria);
  Multiplexer #(.select(3), .width(8), .disabled(0)) multiplexer_2 (
    .in0(8'h1), .in1(8'h2), .in2(8'h4), .in3(8'h8), .in4(8'h10), .in5(8'h20), .in6(8'h40), .in7(8'h80),
    .out(out_4), .sel(counter_1_q), .en(not_1_out));
endmodule

module random_mondo (
  output [7:0] out_1,
  output [7:0] out_2,
  output [7:0] out_3,
  output [7:0] out_4,
  output [7:0] out_5,
  output [7:0] out_6,
  output [7:0] out_7,
  output [7:0] out_8,
  output [7:0] out_9,
  output [7:0] out_10,
  output [7:0] out_11,
  output [7:0] out_12,
  output [7:0] out_13,
  output [7:0] out_14,
  output [7:0] out_15,
  output [7:0] out_16
);

  wire and_1_out, clock_1_out, comparator_1_eq;
  wire [1:0] counter_1_q;
  wire [2:0] multiplexer_2_out, random_1_out;
  wire [7:0] multiplexer_1_out;

  Clock clock_1 (.out(clock_1_out));
  Comparator #(.width(2)) comparator_1 (.a(2'b00), .b(counter_1_q), .eq(comparator_1_eq));  // open: gt, lt
  and and_1 (and_1_out, clock_1_out, comparator_1_eq);
  Random #(.width(3)) random_1 (.clk(and_1_out), .out(random_1_out));  // open: next, clr
  Counter #(.width(2), .max('h3)) counter_1 (.Q(counter_1_q), .clk(clock_1_out));  // open: load, D, count, carry, clr
  Multiplexer #(.select(3), .width(8), .disabled(0)) multiplexer_1 (
    .in0(8'h7), .in1(8'h38), .in2(8'he0), .in3(8'hf0), .in4(8'hf), .in5(8'hc3), .in6({8{1'b0}}),
    .in7({8{1'b0}}), .out(multiplexer_1_out), .sel(multiplexer_2_out));  // open: en
  Multiplexer #(.width(3)) multiplexer_2 (
    .in0(3'b111), .in1(random_1_out), .out(multiplexer_2_out), .sel(comparator_1_eq));  // open: en
  Register register_1 (.D(multiplexer_1_out), .Q(out_1), .clk(clock_1_out));  // open: en, clr
  Register register_2 (.D(out_1), .Q(out_2), .clk(clock_1_out));  // open: en, clr
  Register register_3 (.D(out_2), .Q(out_3), .clk(clock_1_out));  // open: en, clr
  Register register_4 (.D(out_3), .Q(out_4), .clk(clock_1_out));  // open: en, clr
  Register register_5 (.D(out_4), .Q(out_5), .clk(clock_1_out));  // open: en, clr
  Register register_6 (.D(out_5), .Q(out_6), .clk(clock_1_out));  // open: en, clr
  Register register_7 (.D(out_6), .Q(out_7), .clk(clock_1_out));  // open: en, clr
  Register register_8 (.D(out_7), .Q(out_8), .clk(clock_1_out));  // open: en, clr
  Register register_9 (.D(out_8), .Q(out_9), .clk(clock_1_out));  // open: en, clr
  Register register_10 (.D(out_9), .Q(out_10), .clk(clock_1_out));  // open: en, clr
  Register register_11 (.D(out_11), .Q(out_12), .clk(clock_1_out));  // open: en, clr
  Register register_12 (.D(out_10), .Q(out_11), .clk(clock_1_out));  // open: en, clr
  Register register_13 (.D(out_13), .Q(out_14), .clk(clock_1_out));  // open: en, clr
  Register register_14 (.D(out_12), .Q(out_13), .clk(clock_1_out));  // open: en, clr
  Register register_15 (.D(out_14), .Q(out_15), .clk(clock_1_out));  // open: en, clr
  Register register_16 (.D(out_15), .Q(out_16), .clk(clock_1_out));  // open: en, clr
endmodule

module game_over (
  input  [7:0] in_1,
  input  [7:0] in_2,
  output out_3
);

  wire and_1_out, and_2_out, and_3_out, and_4_out, and_5_out, and_6_out, and_7_out, and_8_out;

  and and_1 (and_1_out, in_1[0], in_2[0]);
  and and_2 (and_2_out, in_1[1], in_2[1]);
  and and_3 (and_3_out, in_1[2], in_2[2]);
  and and_4 (and_4_out, in_1[3], in_2[3]);
  and and_5 (and_5_out, in_1[4], in_2[4]);
  and and_6 (and_6_out, in_1[5], in_2[5]);
  and and_7 (and_7_out, in_1[6], in_2[6]);
  and and_8 (and_8_out, in_1[7], in_2[7]);
  or or_1 (out_3, and_1_out, and_2_out, and_3_out, and_4_out, and_5_out, and_6_out, and_7_out, and_8_out);
endmodule

module Fin (
  output [7:0] out_1,
  output [7:0] out_2,
  output [7:0] out_3,
  output [7:0] out_4,
  output [7:0] out_5,
  output [7:0] out_6,
  output [7:0] out_7,
  output [7:0] out_8,
  output [7:0] out_9,
  output [7:0] out_10,
  output [7:0] out_11,
  output [7:0] out_12,
  output [7:0] out_13,
  output [7:0] out_14,
  output [7:0] out_15,
  output [7:0] out_16
);

  DotMatrix #(.matrixcols(16), .matrixrows(8)) dotmatrix_1 (
    .col0({8{1'b1}}), .col1(8'h90), .col2(8'h90), .col3(8'h80), .col4(8'h80), .col5({8{1'b0}}),
    .col6({8{1'b0}}), .col7({8{1'b1}}), .col8({8{1'b0}}), .col9({8{1'b0}}), .col10({8{1'b1}}), .col11(8'h70),
    .col12(8'h38), .col13(8'h1c), .col14(8'he), .col15({8{1'b1}}));

  assign out_1 = {8{1'b1}};
  assign out_2 = 8'he;
  assign out_3 = 8'h1c;
  assign out_4 = 8'h38;
  assign out_5 = 8'h70;
  assign out_6 = {8{1'b1}};
  assign out_7 = {8{1'b0}};
  assign out_8 = {8{1'b0}};
  assign out_9 = {8{1'b1}};
  assign out_10 = {8{1'b0}};
  assign out_11 = {8{1'b0}};
  assign out_12 = 8'h80;
  assign out_13 = 8'h80;
  assign out_14 = 8'h90;
  assign out_15 = 8'h90;
  assign out_16 = {8{1'b1}};
endmodule

module multiplexers (
  input  VINTO,
  input  RESET,
  input  PERSO,
  output [7:0] out_4,
  output [7:0] out_5,
  output [7:0] out_6,
  output [7:0] out_7,
  output [7:0] out_8,
  output [7:0] out_9,
  output [7:0] out_10,
  output [7:0] out_11,
  output [7:0] out_12,
  output [7:0] out_13,
  output [7:0] out_14,
  output [7:0] out_15,
  output [7:0] out_16,
  output [7:0] out_17,
  output [7:0] out_18,
  output [7:0] out_19
);

  wire and_1_out, clock_1_out, d_ff_1_q, not_1_out;
  wire [1:0] d_ff_3_q;
  wire [7:0] fin_1_out_1, fin_1_out_2, fin_1_out_3, fin_1_out_4, fin_1_out_5, fin_1_out_6, fin_1_out_7,
       fin_1_out_8, fin_1_out_9, fin_1_out_10, fin_1_out_11, fin_1_out_12, fin_1_out_13, fin_1_out_14,
       fin_1_out_15, fin_1_out_16, random_mondo_1_out_1, random_mondo_1_out_2, random_mondo_1_out_3,
       random_mondo_1_out_4, random_mondo_1_out_5, random_mondo_1_out_6, random_mondo_1_out_7,
       random_mondo_1_out_8, random_mondo_1_out_9, random_mondo_1_out_10, random_mondo_1_out_11,
       random_mondo_1_out_12, random_mondo_1_out_13, random_mondo_1_out_14, random_mondo_1_out_15,
       random_mondo_1_out_16, vittoria_1_out_1, vittoria_1_out_2, vittoria_1_out_3, vittoria_1_out_4,
       vittoria_1_out_5, vittoria_1_out_6, vittoria_1_out_7, vittoria_1_out_8, vittoria_1_out_9,
       vittoria_1_out_10, vittoria_1_out_11, vittoria_1_out_12, vittoria_1_out_13, vittoria_1_out_14,
       vittoria_1_out_15, vittoria_1_out_16;

  vittoria vittoria_1 (
    .out_1(vittoria_1_out_1), .out_2(vittoria_1_out_2), .out_3(vittoria_1_out_3), .out_4(vittoria_1_out_4),
    .out_5(vittoria_1_out_5), .out_6(vittoria_1_out_6), .out_7(vittoria_1_out_7), .out_8(vittoria_1_out_8),
    .out_9(vittoria_1_out_9), .out_10(vittoria_1_out_10), .out_11(vittoria_1_out_11),
    .out_12(vittoria_1_out_12), .out_13(vittoria_1_out_13), .out_14(vittoria_1_out_14),
    .out_15(vittoria_1_out_15), .out_16(vittoria_1_out_16));
  Clock clock_1 (.out(clock_1_out));
  D_Flip_Flop d_ff_1 (.clk(clock_1_out), .D(VINTO), .Q(d_ff_1_q));  // open: Qn, preset, en, reset
  Fin fin_1 (
    .out_1(fin_1_out_1), .out_2(fin_1_out_2), .out_3(fin_1_out_3), .out_4(fin_1_out_4), .out_5(fin_1_out_5),
    .out_6(fin_1_out_6), .out_7(fin_1_out_7), .out_8(fin_1_out_8), .out_9(fin_1_out_9),
    .out_10(fin_1_out_10), .out_11(fin_1_out_11), .out_12(fin_1_out_12), .out_13(fin_1_out_13),
    .out_14(fin_1_out_14), .out_15(fin_1_out_15), .out_16(fin_1_out_16));
  not not_1 (not_1_out, d_ff_1_q);
  and and_1 (and_1_out, clock_1_out, not_1_out);
  random_mondo random_mondo_1 (
    .out_1(random_mondo_1_out_1), .out_2(random_mondo_1_out_2), .out_3(random_mondo_1_out_3),
    .out_4(random_mondo_1_out_4), .out_5(random_mondo_1_out_5), .out_6(random_mondo_1_out_6),
    .out_7(random_mondo_1_out_7), .out_8(random_mondo_1_out_8), .out_9(random_mondo_1_out_9),
    .out_10(random_mondo_1_out_10), .out_11(random_mondo_1_out_11), .out_12(random_mondo_1_out_12),
    .out_13(random_mondo_1_out_13), .out_14(random_mondo_1_out_14), .out_15(random_mondo_1_out_15),
    .out_16(random_mondo_1_out_16));
  D_Flip_Flop d_ff_2 (.clk(and_1_out), .D(VINTO), .Q(d_ff_3_q[1]), .reset(RESET));  // open: Qn, preset, en
  D_Flip_Flop d_ff_3 (.clk(and_1_out), .D(PERSO), .Q(d_ff_3_q[0]), .reset(RESET));  // open: Qn, preset, en
  Multiplexer #(.select(2), .width(8), .disabled(0)) multiplexer_1 (
    .in0(random_mondo_1_out_1), .in1(fin_1_out_1), .in2(vittoria_1_out_1), .out(out_4), .sel(d_ff_3_q));  // open: in3, en
  Multiplexer #(.select(2), .width(8), .disabled(0)) multiplexer_2 (
    .in0(random_mondo_1_out_2), .in1(fin_1_out_2), .in2(vittoria_1_out_2), .out(out_5), .sel(d_ff_3_q));  // open: in3, en
  Multiplexer #(.select(2), .width(8), .disabled(0)) multiplexer_3 (
    .in0(random_mondo_1_out_3), .in1(fin_1_out_3), .in2(vittoria_1_out_3), .out(out_6), .sel(d_ff_3_q));  // open: in3, en
  Multiplexer #(.select(2), .width(8), .disabled(0)) multiplexer_4 (
    .in0(random_mondo_1_out_4), .in1(fin_1_out_4), .in2(vittoria_1_out_4), .out(out_7), .sel(d_ff_3_q));  // open: in3, en
  Multiplexer #(.select(2), .width(8), .disabled(0)) multiplexer_5 (
    .in0(random_mondo_1_out_5), .in1(fin_1_out_5), .in2(vittoria_1_out_5), .out(out_8), .sel(d_ff_3_q));  // open: in3, en
  Multiplexer #(.select(2), .width(8), .disabled(0)) multiplexer_6 (
    .in0(random_mondo_1_out_6), .in1(fin_1_out_6), .in2(vittoria_1_out_6), .out(out_9), .sel(d_ff_3_q));  // open: in3, en
  Multiplexer #(.select(2), .width(8), .disabled(0)) multiplexer_7 (
    .in0(random_mondo_1_out_7), .in1(fin_1_out_7), .in2(vittoria_1_out_7), .out(out_10), .sel(d_ff_3_q));  // open: in3, en
  Multiplexer #(.select(2), .width(8), .disabled(0)) multiplexer_8 (
    .in0(random_mondo_1_out_8), .in1(fin_1_out_8), .in2(vittoria_1_out_8), .out(out_11), .sel(d_ff_3_q));  // open: in3, en
  Multiplexer #(.select(2), .width(8), .disabled(0)) multiplexer_9 (
    .in0(random_mondo_1_out_9), .in1(fin_1_out_9), .in2(vittoria_1_out_9), .out(out_12), .sel(d_ff_3_q));  // open: in3, en
  Multiplexer #(.select(2), .width(8), .disabled(0)) multiplexer_10 (
    .in0(random_mondo_1_out_10), .in1(fin_1_out_10), .in2(vittoria_1_out_10), .out(out_13), .sel(d_ff_3_q));  // open: in3, en
  Multiplexer #(.select(2), .width(8), .disabled(0)) multiplexer_11 (
    .in0(random_mondo_1_out_11), .in1(fin_1_out_11), .in2(vittoria_1_out_11), .out(out_14), .sel(d_ff_3_q));  // open: in3, en
  Multiplexer #(.select(2), .width(8), .disabled(0)) multiplexer_12 (
    .in0(random_mondo_1_out_12), .in1(fin_1_out_12), .in2(vittoria_1_out_12), .out(out_15), .sel(d_ff_3_q));  // open: in3, en
  Multiplexer #(.select(2), .width(8), .disabled(0)) multiplexer_13 (
    .in0(random_mondo_1_out_13), .in1(fin_1_out_13), .in2(vittoria_1_out_13), .out(out_16), .sel(d_ff_3_q));  // open: in3, en
  Multiplexer #(.select(2), .width(8), .disabled(0)) multiplexer_14 (
    .in0(random_mondo_1_out_14), .in1(fin_1_out_14), .in2(vittoria_1_out_14), .out(out_17), .sel(d_ff_3_q));  // open: in3, en
  Multiplexer #(.select(2), .width(8), .disabled(0)) multiplexer_15 (
    .in0(random_mondo_1_out_15), .in1(fin_1_out_15), .in2(vittoria_1_out_15), .out(out_18), .sel(d_ff_3_q));  // open: in3, en
  Multiplexer #(.select(2), .width(8), .disabled(0)) multiplexer_16 (
    .in0(random_mondo_1_out_16), .in1(fin_1_out_16), .in2(vittoria_1_out_16), .out(out_19), .sel(d_ff_3_q));  // open: in3, en
endmodule

module punti (
  input  [7:0] in_1,
  output [7:0] out_2,
  output [7:0] out_3,
  output [7:0] out_4,
  output [7:0] out_5,
  output [7:0] out_6,
  output [7:0] out_7
);

  Multiplexer #(.select(4), .width(8)) multiplexer_1 (
    .in0({8{1'b1}}), .in1({8{1'b0}}), .in2(8'hcf), .in3(8'hc3), .in4(8'hf8), .in5(8'hfb), .in6({8{1'b1}}),
    .in7(8'hc0), .in8({8{1'b1}}), .in9(8'hfb), .out(out_2), .sel(in_1[3:0]));  // open: in10, in11, in12, in13, in14, in15, en
  Multiplexer #(.select(4), .width(8)) multiplexer_2 (
    .in0({8{1'b1}}), .in1({8{1'b0}}), .in2(8'hcf), .in3(8'hc3), .in4(8'hf8), .in5(8'hfb), .in6({8{1'b1}}),
    .in7(8'hc0), .in8({8{1'b1}}), .in9(8'hfb), .out(out_3), .sel(in_1[3:0]));  // open: in10, in11, in12, in13, in14, in15, en
  Multiplexer #(.select(4), .width(8)) multiplexer_3 (
    .in0(8'hc3), .in1({8{1'b1}}), .in2(8'hdb), .in3(8'hdb), .in4(8'h18), .in5(8'hdb), .in6(8'hdb),
    .in7(8'hc0), .in8(8'hdb), .in9(8'hdb), .out(out_4), .sel(in_1[3:0]));  // open: in10, in11, in12, in13, in14, in15, en
  Multiplexer #(.select(4), .width(8)) multiplexer_4 (
    .in0(8'hc3), .in1({8{1'b1}}), .in2(8'hdb), .in3(8'hdb), .in4(8'h18), .in5(8'hdb), .in6(8'hdb),
    .in7(8'hc0), .in8(8'hdb), .in9(8'hdb), .out(out_5), .sel(in_1[3:0]));  // open: in10, in11, in12, in13, in14, in15, en
  Multiplexer #(.select(4), .width(8)) multiplexer_5 (
    .in0({8{1'b1}}), .in1({8{1'b0}}), .in2(8'hf3), .in3({8{1'b1}}), .in4({8{1'b1}}), .in5(8'hdf),
    .in6(8'hdf), .in7({8{1'b1}}), .in8({8{1'b1}}), .in9({8{1'b1}}), .out(out_6), .sel(in_1[3:0]));  // open: in10, in11, in12, in13, in14, in15, en
  Multiplexer #(.select(4), .width(8)) multiplexer_6 (
    .in0({8{1'b1}}), .in1({8{1'b0}}), .in2(8'hf3), .in3({8{1'b1}}), .in4({8{1'b1}}), .in5(8'hdf),
    .in6(8'hdf), .in7({8{1'b1}}), .in8({8{1'b1}}), .in9({8{1'b1}}), .out(out_7), .sel(in_1[3:0]));  // open: in10, in11, in12, in13, in14, in15, en
endmodule

module contatori (
  input  in_1,
  input  [7:0] in_2,
  output out_3,
  output [7:0] out_4,
  output [7:0] out_5
);

  wire comparator_1_eq, comparator_2_eq, comparator_3_eq, passato_1_out_3;

  passato passato_1 (.in_1({8{1'b1}}), .in_2(in_2), .out_3(passato_1_out_3));
  Counter #(.max('h9)) counter_1 (.Q(out_4), .clk(passato_1_out_3), .clr(in_1));  // open: load, D, count, carry
  Counter #(.max('h9)) counter_2 (.Q(out_5), .clk(comparator_1_eq), .clr(in_1));  // open: load, D, count, carry
  Comparator comparator_1 (.a(out_4), .b({8{1'b0}}), .eq(comparator_1_eq));  // open: gt, lt
  Comparator comparator_2 (.a(out_5), .b(8'h1), .eq(comparator_2_eq));  // open: gt, lt
  and and_1 (out_3, comparator_2_eq, comparator_3_eq);
  Comparator comparator_3 (.a(out_4), .b({8{1'b0}}), .eq(comparator_3_eq));  // open: gt, lt
endmodule

module passato (
  input  [7:0] in_1,
  input  [7:0] in_2,
  output out_3
);

  wire and_1_out, and_2_out, and_3_out, and_4_out, and_5_out, and_6_out;

  and and_1 (and_1_out, in_1[0], in_2[0]);
  and and_2 (and_2_out, in_1[1], in_2[1]);
  and and_3 (and_3_out, in_1[2], in_2[2]);
  and and_4 (and_4_out, in_1[3], in_2[3]);
  and and_5 (and_5_out, in_1[5], in_2[5]);
  and and_6 (and_6_out, in_1[6], in_2[6]);
  or or_1 (out_3, and_1_out, and_2_out, and_3_out, and_4_out, and_5_out, and_6_out);
endmodule

module vittoria (
  output [7:0] out_1,
  output [7:0] out_2,
  output [7:0] out_3,
  output [7:0] out_4,
  output [7:0] out_5,
  output [7:0] out_6,
  output [7:0] out_7,
  output [7:0] out_8,
  output [7:0] out_9,
  output [7:0] out_10,
  output [7:0] out_11,
  output [7:0] out_12,
  output [7:0] out_13,
  output [7:0] out_14,
  output [7:0] out_15,
  output [7:0] out_16
);

  DotMatrix #(.matrixcols(16), .matrixrows(8)) dotmatrix_1 (
    .col0(8'h20), .col1(8'h70), .col2(8'h20), .col3(8'h3), .col4(8'h3), .col5(8'h7), .col6(8'h7),
    .col7({8{1'b1}}), .col8(8'he7), .col9(8'he7), .col10(8'he7), .col11(8'h3), .col12(8'h3), .col13(8'h8),
    .col14(8'h1c), .col15(8'h8));

  assign out_1 = 8'h8;
  assign out_2 = 8'h1c;
  assign out_3 = 8'h8;
  assign out_4 = 8'h3;
  assign out_5 = 8'h3;
  assign out_6 = 8'he7;
  assign out_7 = 8'he7;
  assign out_8 = 8'he7;
  assign out_9 = {8{1'b1}};
  assign out_10 = 8'h7;
  assign out_11 = 8'h7;
  assign out_12 = 8'h3;
  assign out_13 = 8'h3;
  assign out_14 = 8'h20;
  assign out_15 = 8'h70;
  assign out_16 = 8'h20;
endmodule
